// Logisim project Datapath.circ as structural Verilog: 14 circuits, main circuit main
module main (
  input  [13:0] in_1,
  output [13:0] out_2
);

  wire alu_1_zero_signal, branch_1_out_4, button_1_out, button_2_out, clock_1_out, clock_manage_1_out_4,
       control_unit_1_alu_src, control_unit_1_eql, control_unit_1_jump, control_unit_1_lw_en,
       control_unit_1_neql, control_unit_1_output, control_unit_1_output_2, control_unit_1_reg_dst,
       control_unit_1_sw_en, control_unit_1_w_en, control_unit_1_wait, or_1_out;
  wire [1:0] control_unit_1_out_6;
  wire [2:0] multiplexer_1_out, split_1_out_3, split_1_out_4, split_1_out_5;
  wire [3:0] n7_segment_1_out_4, n7_segment_1_out_5, n7_segment_1_out_6, n7_segment_2_out_4,
       n7_segment_2_out_5, n7_segment_2_out_6;
  wire [4:0] control_unit_1_out_2, split_1_out_6;
  wire [5:0] n7_segment_1_out_3, n7_segment_2_out_3;
  wire [8:0] split_1_out_2;
  wire [12:0] n7_segment_1_out_7, n7_segment_2_out_7;
  wire [13:0] adder_1_out, adder_2_out, alu_1_result, bit_extender_1_out, bit_extender_2_out,
       multiplexer_2_out, multiplexer_3_out, multiplexer_4_out, multiplexer_5_out, ram_1_data, register_1_q,
       register_file_1_out_8, rom_1_data;

  Button button_1 (.out(button_1_out));
  Button button_2 (.out(button_2_out));
  Clock clock_1 (.out(clock_1_out));
  DotMatrix #(.inputtype("row"), .matrixcols(13), .matrixrows(2)) dotmatrix_1 (
    .row0(n7_segment_1_out_7), .row1(n7_segment_1_out_7));
  Hex_Digit_Display hex_digit_display_1 (.value(n7_segment_1_out_4));  // open: dp
  DotMatrix #(.matrixcols(1), .matrixrows(6)) dotmatrix_2 (.col0(n7_segment_1_out_3));
  _7_segment u_7_segment_1 (
    .in_1(in_1), .out_4(n7_segment_1_out_4), .out_5(n7_segment_1_out_5), .out_6(n7_segment_1_out_6),
    .out_3(n7_segment_1_out_3), .out_7(n7_segment_1_out_7), .in_2(control_unit_1_output_2));
  Hex_Digit_Display hex_digit_display_2 (.value(n7_segment_1_out_5));  // open: dp
  Hex_Digit_Display hex_digit_display_3 (.value(n7_segment_1_out_6));  // open: dp
  Register #(.width(14)) register_1 (
    .D(multiplexer_4_out), .Q(register_1_q), .clk(clock_manage_1_out_4), .clr(button_2_out));  // open: en
  // Probe on in_1
  clock_manage clock_manage_1 (
    .Clock(clock_1_out), .Wait_Enable(control_unit_1_wait), .Resleae(button_1_out),
    .out_4(clock_manage_1_out_4));
  Adder #(.width(14)) adder_1 (.a(register_1_q), .b(14'h1), .out(adder_1_out));  // open: cin, cout
  Split split_1 (
    .in_1(rom_1_data), .out_3(split_1_out_3), .out_4(split_1_out_4), .out_5(split_1_out_5),
    .out_6(split_1_out_6), .out_2(split_1_out_2));
  ROM #(.addrWidth(14), .dataWidth(14)) rom_1 (.addr(register_1_q), .data(rom_1_data));  // open: sel
  Control_Unit control_unit_1 (
    .Input(split_1_out_6), .out_2(control_unit_1_out_2), .w_en(control_unit_1_w_en),
    .reg_dst(control_unit_1_reg_dst), .alu_src(control_unit_1_alu_src), .out_6(control_unit_1_out_6),
    .sw_en(control_unit_1_sw_en), .lw_en(control_unit_1_lw_en), .eql(control_unit_1_eql),
    .neql(control_unit_1_neql), .jump(control_unit_1_jump), .Output(control_unit_1_output),
    .Output_2(control_unit_1_output_2), .\wait (control_unit_1_wait));
  assign bit_extender_1_out = {{5{1'b0}}, split_1_out_2};  // Bit_Extender bit_extender_1
  Multiplexer #(.width(3), .enable("false")) multiplexer_1 (
    .in0(split_1_out_3), .in1(split_1_out_4), .out(multiplexer_1_out), .sel(control_unit_1_reg_dst));
  DotMatrix #(.inputtype("row"), .matrixcols(13), .matrixrows(2)) dotmatrix_3 (
    .row0(n7_segment_2_out_7), .row1(n7_segment_2_out_7));
  Register_File register_file_1 (
    .in_1(multiplexer_5_out), .Write_Enable(control_unit_1_w_en), .Select_Bit(multiplexer_1_out),
    .Clock(clock_manage_1_out_4), .Reset_Register(button_2_out), .Read_Register_1(split_1_out_5),
    .Read_register_2(split_1_out_4), .out_8(register_file_1_out_8), .out_9(out_2));
  assign bit_extender_2_out = {{11{1'b0}}, split_1_out_3};  // Bit_Extender bit_extender_2
  DotMatrix #(.matrixcols(1), .matrixrows(6)) dotmatrix_4 (.col0(n7_segment_2_out_3));
  Hex_Digit_Display hex_digit_display_4 (.value(n7_segment_2_out_5));  // open: dp
  Hex_Digit_Display hex_digit_display_5 (.value(n7_segment_2_out_4));  // open: dp
  _7_segment u_7_segment_2 (
    .in_1(out_2), .out_4(n7_segment_2_out_4), .out_5(n7_segment_2_out_5), .out_6(n7_segment_2_out_6),
    .out_3(n7_segment_2_out_3), .out_7(n7_segment_2_out_7), .in_2(control_unit_1_output));
  Hex_Digit_Display hex_digit_display_6 (.value(n7_segment_2_out_6));  // open: dp
  Multiplexer #(.width(14), .enable("false")) multiplexer_2 (
    .in0(out_2), .in1(bit_extender_2_out), .out(multiplexer_2_out), .sel(control_unit_1_alu_src));
  // Probe on out_2
  Adder #(.width(14)) adder_2 (.a(adder_1_out), .b(bit_extender_2_out), .out(adder_2_out));  // open: cin, cout
  Branch branch_1 (
    .in_1(control_unit_1_eql), .in_2(alu_1_zero_signal), .in_3(control_unit_1_neql), .out_4(branch_1_out_4));
  ALU alu_1 (
    .ALU_Opcode(control_unit_1_out_2), .B(multiplexer_2_out), .A(register_file_1_out_8),
    .Result(alu_1_result), .Zero_SIgnal(alu_1_zero_signal));
  Multiplexer #(.width(14), .enable("false")) multiplexer_3 (
    .in0(adder_1_out), .in1(adder_2_out), .out(multiplexer_3_out), .sel(branch_1_out_4));
  Multiplexer #(.width(14), .enable("false")) multiplexer_4 (
    .in0(multiplexer_3_out), .in1(bit_extender_1_out), .out(multiplexer_4_out), .sel(control_unit_1_jump));
  or or_1 (or_1_out, control_unit_1_sw_en, control_unit_1_lw_en);
  RAM #(.addrWidth(14), .dataWidth(14), .bus("separate")) ram_1 (
    .addr(alu_1_result), .din(out_2), .data(ram_1_data), .str(control_unit_1_sw_en), .sel(or_1_out),
    .clk(clock_manage_1_out_4), .ld(control_unit_1_lw_en));  // open: clr
  Multiplexer #(.select(2), .width(14), .enable("false")) multiplexer_5 (
    .in0(alu_1_result), .in1(ram_1_data), .in2(in_1), .in3(in_1), .out(multiplexer_5_out),
    .sel(control_unit_1_out_6));

  // Notes on the sheet:
  //   Keyboard
  //   OK button
  //   Reboot
  //   Clock
  //   CSE332 section2
  //   Group-4
  //   INPUT
  //   Decimal
  //   contents of rom_1 (hex, n*v repeats v):
  //   1c09 1c5a 47 1c63 e3 2218 801 802 125c 1624 8a 249 2210 1a08 1fd5 2238 2210
  //   OUTPUT
  //   Decimal
  //   Binary
endmodule

module one_bit_ALU (
  input  A,
  input  B,
  input  Cin,
  input  [1:0] select_bit,
  output Res,
  output Cout
);

  wire adder_one_bit_1_s, and_1_out, or_1_out, xor_1_out;

  and and_1 (and_1_out, A, B);
  or or_1 (or_1_out, A, B);
  xor xor_1 (xor_1_out, A, B);
  adder_one_bit adder_one_bit_1 (.A(A), .B(B), .Cin(Cin), .S(adder_one_bit_1_s), .Cout(Cout));
  Multiplexer #(.select(2), .enable("false")) multiplexer_1 (
    .in0(and_1_out), .in1(or_1_out), .in2(xor_1_out), .in3(adder_one_bit_1_s), .out(Res), .sel(select_bit));
endmodule

module adder_one_bit (
  input  A,
  input  B,
  input  Cin,
  output S,
  output Cout
);

  wire and_1_out, and_2_out, xor_1_out;

  xor xor_1 (xor_1_out, A, B);
  xor xor_2 (S, xor_1_out, Cin);
  and and_1 (and_1_out, xor_1_out, Cin);
  and and_2 (and_2_out, A, B);
  or or_1 (Cout, and_1_out, and_2_out);
endmodule

module ALU (
  input  [13:0] B,
  input  [13:0] A,
  input  [4:0] ALU_Opcode,
  output Zero_SIgnal,
  output [13:0] Result
);

  wire not_2_out, one_bit_alu_1_cout, one_bit_alu_2_cout, one_bit_alu_3_cout, one_bit_alu_4_cout,
       one_bit_alu_5_cout, one_bit_alu_6_cout, one_bit_alu_7_cout, one_bit_alu_8_cout, one_bit_alu_9_cout,
       one_bit_alu_10_cout, one_bit_alu_11_cout, one_bit_alu_12_cout, one_bit_alu_13_cout,
       one_bit_alu_14_cout, or_1_out;
  wire [1:1] and_1_out;
  wire [13:0] bit_extender_1_out, multiplexer_1_out, not_1_out, one_bit_alu_1_res, shifter_1_output;

  assign not_1_out = ~B;  // NOT_Gate not_1, 14 bits wide
  Multiplexer #(.width(14), .enable("false")) multiplexer_1 (
    .in0(B), .in1(not_1_out), .out(multiplexer_1_out), .sel(ALU_Opcode[2]));
  one_bit_ALU one_bit_alu_1 (
    .Cin(ALU_Opcode[2]), .select_bit(ALU_Opcode[4:3]), .Res(one_bit_alu_1_res[0]), .Cout(one_bit_alu_1_cout),
    .A(A[0]), .B(multiplexer_1_out[0]));
  one_bit_ALU one_bit_alu_2 (
    .Cin(one_bit_alu_1_cout), .select_bit(ALU_Opcode[4:3]), .Res(one_bit_alu_1_res[1]),
    .Cout(one_bit_alu_2_cout), .A(A[1]), .B(multiplexer_1_out[1]));
  one_bit_ALU one_bit_alu_3 (
    .Cin(one_bit_alu_2_cout), .select_bit(ALU_Opcode[4:3]), .Res(one_bit_alu_1_res[2]),
    .Cout(one_bit_alu_3_cout), .A(A[2]), .B(multiplexer_1_out[2]));
  one_bit_ALU one_bit_alu_4 (
    .Cin(one_bit_alu_3_cout), .select_bit(ALU_Opcode[4:3]), .Res(one_bit_alu_1_res[3]),
    .Cout(one_bit_alu_4_cout), .A(A[3]), .B(multiplexer_1_out[3]));
  one_bit_ALU one_bit_alu_5 (
    .Cin(one_bit_alu_4_cout), .select_bit(ALU_Opcode[4:3]), .Res(one_bit_alu_1_res[4]),
    .Cout(one_bit_alu_5_cout), .A(A[4]), .B(multiplexer_1_out[4]));
  one_bit_ALU one_bit_alu_6 (
    .Cin(one_bit_alu_5_cout), .select_bit(ALU_Opcode[4:3]), .Res(one_bit_alu_1_res[5]),
    .Cout(one_bit_alu_6_cout), .A(A[5]), .B(multiplexer_1_out[5]));
  one_bit_ALU one_bit_alu_7 (
    .Cin(one_bit_alu_6_cout), .select_bit(ALU_Opcode[4:3]), .Res(one_bit_alu_1_res[6]),
    .Cout(one_bit_alu_7_cout), .A(A[6]), .B(multiplexer_1_out[6]));
  one_bit_ALU one_bit_alu_8 (
    .Cin(one_bit_alu_7_cout), .select_bit(ALU_Opcode[4:3]), .Res(one_bit_alu_1_res[7]),
    .Cout(one_bit_alu_8_cout), .A(A[7]), .B(multiplexer_1_out[7]));
  one_bit_ALU one_bit_alu_9 (
    .Cin(one_bit_alu_8_cout), .select_bit(ALU_Opcode[4:3]), .Res(one_bit_alu_1_res[8]),
    .Cout(one_bit_alu_9_cout), .A(A[8]), .B(multiplexer_1_out[8]));
  one_bit_ALU one_bit_alu_10 (
    .Cin(one_bit_alu_9_cout), .select_bit(ALU_Opcode[4:3]), .Res(one_bit_alu_1_res[9]),
    .Cout(one_bit_alu_10_cout), .A(A[9]), .B(multiplexer_1_out[9]));
  one_bit_ALU one_bit_alu_11 (
    .Cin(one_bit_alu_10_cout), .select_bit(ALU_Opcode[4:3]), .Res(one_bit_alu_1_res[10]),
    .Cout(one_bit_alu_11_cout), .A(A[10]), .B(multiplexer_1_out[10]));
  one_bit_ALU one_bit_alu_12 (
    .Cin(one_bit_alu_11_cout), .select_bit(ALU_Opcode[4:3]), .Res(one_bit_alu_1_res[11]),
    .Cout(one_bit_alu_12_cout), .A(A[11]), .B(multiplexer_1_out[11]));
  one_bit_ALU one_bit_alu_13 (
    .Cin(one_bit_alu_12_cout), .select_bit(ALU_Opcode[4:3]), .Res(one_bit_alu_1_res[12]),
    .Cout(one_bit_alu_13_cout), .A(A[12]), .B(multiplexer_1_out[12]));
  one_bit_ALU one_bit_alu_14 (
    .Cin(one_bit_alu_13_cout), .select_bit(ALU_Opcode[4:3]), .Res(one_bit_alu_1_res[13]),
    .Cout(one_bit_alu_14_cout), .A(A[13]), .B(multiplexer_1_out[13]));
  Shifter shifter_1 (.Data(A), .Shift_amount(B), .in_3(ALU_Opcode[0]), .\output (shifter_1_output));
  Multiplexer #(.select(2), .width(14), .enable("false")) multiplexer_2 (
    .in0(one_bit_alu_1_res), .in1(shifter_1_output), .in2(bit_extender_1_out), .in3(bit_extender_1_out),
    .out(Result), .sel({and_1_out[1], ALU_Opcode[1]}));
  not not_2 (not_2_out, ALU_Opcode[1]);
  and and_1 (and_1_out[1], not_2_out, ALU_Opcode[0]);
  assign bit_extender_1_out = {{13{1'b0}}, one_bit_alu_1_res[13]};  // Bit_Extender bit_extender_1
  or or_1 (or_1_out, Result[0], Result[1], Result[2], Result[3], Result[4], Result[5], Result[6], Result[7], Result[8], Result[9], Result[10], Result[11], Result[12], Result[13]);
  not not_3 (Zero_SIgnal, or_1_out);
endmodule

module Register_File (
  input  [13:0] in_1,
  input  [2:0] Read_Register_1,
  input  Write_Enable,
  input  [2:0] Select_Bit,
  input  [2:0] Read_register_2,
  input  Clock,
  input  Reset_Register,
  output [13:0] out_8,
  output [13:0] out_9
);

  wire demultiplexer_1_out1, demultiplexer_1_out2, demultiplexer_1_out3, demultiplexer_1_out4,
       demultiplexer_1_out5, demultiplexer_1_out6, demultiplexer_1_out7;
  wire [13:0] register_1_q, register_2_q, register_3_q, register_4_q, register_5_q, register_6_q,
       register_7_q;

  Demultiplexer #(.select(3), .enable("false")) demultiplexer_1 (
    .out1(demultiplexer_1_out1), .out2(demultiplexer_1_out2), .out3(demultiplexer_1_out3),
    .out4(demultiplexer_1_out4), .out5(demultiplexer_1_out5), .out6(demultiplexer_1_out6),
    .out7(demultiplexer_1_out7), .in(Write_Enable), .sel(Select_Bit));  // open: out0
  Register #(.width(14)) register_1 (
    .D(in_1), .en(demultiplexer_1_out1), .Q(register_1_q), .clk(Clock), .clr(Reset_Register));
  Register #(.width(14)) register_2 (
    .D(in_1), .en(demultiplexer_1_out2), .Q(register_2_q), .clk(Clock), .clr(Reset_Register));
  Register #(.width(14)) register_3 (
    .D(in_1), .en(demultiplexer_1_out3), .Q(register_3_q), .clk(Clock), .clr(Reset_Register));
  Register #(.width(14)) register_4 (
    .D(in_1), .en(demultiplexer_1_out4), .Q(register_4_q), .clk(Clock), .clr(Reset_Register));
  Register #(.width(14)) register_5 (
    .D(in_1), .en(demultiplexer_1_out5), .Q(register_5_q), .clk(Clock), .clr(Reset_Register));
  Register #(.width(14)) register_6 (
    .D(in_1), .en(demultiplexer_1_out6), .Q(register_6_q), .clk(Clock), .clr(Reset_Register));
  Register #(.width(14)) register_7 (
    .D(in_1), .en(demultiplexer_1_out7), .Q(register_7_q), .clk(Clock), .clr(Reset_Register));
  Multiplexer #(.select(3), .width(14), .enable("false")) multiplexer_1 (
    .in0({14{1'b0}}), .in1(register_1_q), .in2(register_2_q), .in3(register_3_q), .in4(register_4_q),
    .in5(register_5_q), .in6(register_6_q), .in7(register_7_q), .out(out_8), .sel(Read_Register_1));
  Multiplexer #(.select(3), .width(14), .enable("false")) multiplexer_2 (
    .in0({14{1'b0}}), .in1(register_1_q), .in2(register_2_q), .in3(register_3_q), .in4(register_4_q),
    .in5(register_5_q), .in6(register_6_q), .in7(register_7_q), .out(out_9), .sel(Read_register_2));
endmodule

module Split (
  input  [13:0] in_1,
  output [8:0] out_2,
  output [2:0] out_3,
  output [2:0] out_4,
  output [2:0] out_5,
  output [4:0] out_6
);


  assign out_2 = in_1[8:0];
  assign out_3 = in_1[2:0];
  assign out_4 = in_1[5:3];
  assign out_5 = in_1[8:6];
  assign out_6 = in_1[13:9];
endmodule

module Shifter (
  input  [13:0] Data,
  input  [13:0] Shift_amount,
  input  in_3,
  output [13:0] \output 
);

  wire [13:0] shifter_1_out, shifter_2_out;

  Shifter_part #(.width(14)) shifter_1 (.in(Data), .\dist (Shift_amount[3:0]), .out(shifter_1_out));
  Shifter_part #(.width(14), .shift("lr")) shifter_2 (.in(Data), .\dist (Shift_amount[3:0]), .out(shifter_2_out));
  Multiplexer #(.width(14), .enable("false")) multiplexer_1 (
    .in0(shifter_1_out), .in1(shifter_2_out), .out(\output ), .sel(in_3));
endmodule

module Control_Unit (
  input  [4:0] Input,
  output [4:0] out_2,
  output w_en,
  output reg_dst,
  output alu_src,
  output [1:0] out_6,
  output sw_en,
  output lw_en,
  output eql,
  output neql,
  output jump,
  output Output,
  output \wait ,
  output Output_2
);

  wire and_1_out, and_2_out, and_3_out, and_4_out, and_5_out, and_6_out, and_7_out, and_8_out, and_9_out,
       and_10_out, and_11_out, and_12_out, and_13_out, and_14_out, and_15_out, and_16_out, and_17_out,
       and_18_out, and_19_out, and_20_out, and_21_out, and_22_out, and_23_out, and_24_out, and_25_out,
       and_26_out, and_27_out, and_28_out, and_29_out, and_30_out, and_31_out, and_32_out, not_1_out,
       not_2_out, not_3_out, not_4_out, not_5_out, not_6_out, not_7_out, not_8_out, not_9_out, not_10_out,
       not_11_out, not_12_out, not_13_out, not_14_out, not_15_out, not_16_out, not_17_out, not_18_out,
       not_19_out, not_20_out, not_21_out, not_22_out, not_23_out, not_24_out, not_25_out, not_26_out,
       not_27_out, not_28_out, not_29_out, not_30_out, not_31_out, not_32_out, not_33_out, not_34_out,
       not_35_out, not_36_out, not_37_out, not_38_out, not_39_out, not_40_out, not_41_out, not_42_out,
       not_43_out, not_44_out, not_45_out, not_46_out, not_47_out, not_48_out, not_49_out, not_50_out,
       not_51_out, not_52_out, not_53_out, not_54_out, not_55_out, not_56_out, not_57_out, not_58_out,
       not_59_out, not_60_out, not_61_out, not_62_out, not_63_out, not_64_out, not_65_out, not_66_out,
       not_67_out, not_68_out, not_69_out, not_70_out, not_71_out, not_72_out, not_73_out, not_74_out,
       not_75_out, not_76_out, not_77_out, not_78_out, not_79_out, not_80_out, not_81_out, not_82_out,
       not_83_out, not_84_out, not_85_out, not_86_out, not_87_out, not_88_out, not_89_out, not_90_out,
       not_91_out, not_92_out, not_93_out, not_94_out, not_95_out, not_96_out, not_97_out, not_98_out,
       not_99_out, not_100_out, not_101_out, or_6_out;

  not not_1 (not_1_out, Input[4]);
  not not_2 (not_2_out, Input[3]);
  and and_1 (and_1_out, not_1_out, not_2_out, Input[2], not_3_out, Input[0]);
  not not_3 (not_3_out, Input[1]);
  not not_4 (not_4_out, Input[4]);
  not not_5 (not_5_out, Input[3]);
  not not_6 (not_6_out, Input[2]);
  not not_7 (not_7_out, Input[4]);
  not not_8 (not_8_out, Input[2]);
  not not_9 (not_9_out, Input[4]);
  not not_10 (not_10_out, Input[0]);
  not not_11 (not_11_out, Input[4]);
  not not_12 (not_12_out, Input[4]);
  not not_13 (not_13_out, Input[0]);
  not not_14 (not_14_out, Input[4]);
  not not_15 (not_15_out, Input[3]);
  not not_16 (not_16_out, Input[2]);
  not not_17 (not_17_out, Input[4]);
  not not_18 (not_18_out, Input[3]);
  not not_19 (not_19_out, Input[1]);
  not not_20 (not_20_out, Input[4]);
  not not_21 (not_21_out, Input[2]);
  not not_22 (not_22_out, Input[4]);
  not not_23 (not_23_out, Input[4]);
  not not_24 (not_24_out, Input[0]);
  not not_25 (not_25_out, Input[4]);
  not not_26 (not_26_out, Input[2]);
  not not_27 (not_27_out, Input[4]);
  not not_28 (not_28_out, Input[2]);
  not not_29 (not_29_out, Input[4]);
  not not_30 (not_30_out, Input[1]);
  not not_31 (not_31_out, Input[0]);
  not not_32 (not_32_out, Input[4]);
  not not_33 (not_33_out, Input[3]);
  not not_34 (not_34_out, Input[4]);
  not not_35 (not_35_out, Input[2]);
  not not_36 (not_36_out, Input[1]);
  not not_37 (not_37_out, Input[0]);
  not not_38 (not_38_out, Input[4]);
  not not_39 (not_39_out, Input[2]);
  not not_40 (not_40_out, Input[1]);
  not not_41 (not_41_out, Input[4]);
  not not_42 (not_42_out, Input[2]);
  not not_43 (not_43_out, Input[0]);
  not not_44 (not_44_out, Input[4]);
  not not_45 (not_45_out, Input[3]);
  not not_46 (not_46_out, Input[0]);
  not not_47 (not_47_out, Input[4]);
  not not_48 (not_48_out, Input[2]);
  not not_49 (not_49_out, Input[1]);
  not not_50 (not_50_out, Input[3]);
  not not_51 (not_51_out, Input[2]);
  not not_52 (not_52_out, Input[1]);
  not not_53 (not_53_out, Input[0]);
  not not_54 (not_54_out, Input[4]);
  not not_55 (not_55_out, Input[3]);
  not not_56 (not_56_out, Input[4]);
  not not_57 (not_57_out, Input[0]);
  not not_58 (not_58_out, Input[4]);
  not not_59 (not_59_out, Input[3]);
  not not_60 (not_60_out, Input[2]);
  not not_61 (not_61_out, Input[4]);
  not not_62 (not_62_out, Input[3]);
  not not_63 (not_63_out, Input[4]);
  not not_64 (not_64_out, Input[2]);
  not not_65 (not_65_out, Input[0]);
  not not_66 (not_66_out, Input[4]);
  not not_67 (not_67_out, Input[3]);
  not not_68 (not_68_out, Input[2]);
  not not_69 (not_69_out, Input[1]);
  not not_70 (not_70_out, Input[4]);
  not not_71 (not_71_out, Input[3]);
  not not_72 (not_72_out, Input[2]);
  not not_73 (not_73_out, Input[4]);
  not not_74 (not_74_out, Input[3]);
  not not_75 (not_75_out, Input[4]);
  not not_76 (not_76_out, Input[2]);
  not not_77 (not_77_out, Input[0]);
  not not_78 (not_78_out, Input[4]);
  not not_79 (not_79_out, Input[3]);
  not not_80 (not_80_out, Input[2]);
  not not_81 (not_81_out, Input[1]);
  not not_82 (not_82_out, Input[0]);
  not not_83 (not_83_out, Input[4]);
  not not_84 (not_84_out, Input[0]);
  not not_85 (not_85_out, Input[4]);
  not not_86 (not_86_out, Input[4]);
  not not_87 (not_87_out, Input[0]);
  not not_88 (not_88_out, Input[4]);
  not not_89 (not_89_out, Input[2]);
  not not_90 (not_90_out, Input[4]);
  not not_91 (not_91_out, Input[1]);
  not not_92 (not_92_out, Input[0]);
  not not_93 (not_93_out, Input[4]);
  not not_94 (not_94_out, Input[1]);
  not not_95 (not_95_out, Input[3]);
  not not_96 (not_96_out, Input[2]);
  not not_97 (not_97_out, Input[1]);
  not not_98 (not_98_out, Input[3]);
  not not_99 (not_99_out, Input[2]);
  not not_100 (not_100_out, Input[1]);
  not not_101 (not_101_out, Input[0]);
  and and_2 (and_2_out, not_4_out, not_5_out, not_6_out);
  and and_3 (and_3_out, not_7_out, not_8_out, Input[0]);
  and and_4 (and_4_out, not_9_out, Input[1], not_10_out);
  and and_5 (and_5_out, not_11_out, Input[3], Input[1]);
  and and_6 (and_6_out, not_12_out, Input[3], Input[2], not_13_out);
  and and_7 (and_7_out, not_14_out, not_15_out, not_16_out);
  and and_8 (and_8_out, not_17_out, not_18_out, not_19_out, Input[0]);
  and and_9 (and_9_out, not_20_out, not_21_out, Input[0]);
  and and_10 (and_10_out, not_22_out, Input[3], Input[1]);
  and and_11 (and_11_out, not_23_out, Input[3], Input[2], not_24_out);
  and and_12 (and_12_out, not_25_out, not_26_out, Input[1]);
  and and_13 (and_13_out, not_27_out, Input[3], not_28_out, Input[0]);
  and and_14 (and_14_out, not_29_out, Input[3], Input[2], not_30_out, not_31_out);
  and and_15 (and_15_out, not_32_out, not_33_out, Input[2], Input[1], Input[0]);
  and and_16 (and_16_out, not_34_out, Input[3], not_35_out, not_36_out, not_37_out);
  and and_17 (and_17_out, not_38_out, Input[3], not_39_out, not_40_out);
  and and_18 (and_18_out, not_41_out, Input[3], not_42_out, not_43_out);
  and and_19 (and_19_out, not_44_out, not_45_out, not_46_out);
  and and_20 (and_20_out, not_47_out, not_48_out, not_49_out);
  and and_21 (and_21_out, not_50_out, not_51_out, not_52_out, not_53_out);
  and and_22 (and_22_out, not_54_out, not_55_out, Input[1]);
  and and_23 (and_23_out, not_56_out, Input[1], not_57_out);
  and and_24 (and_24_out, not_58_out, not_59_out, not_60_out, Input[0]);
  and and_25 (and_25_out, not_61_out, not_62_out, Input[1], Input[0]);
  and and_26 (and_26_out, not_63_out, Input[3], not_64_out, not_65_out);
  and and_27 (and_27_out, not_66_out, Input[3], Input[2], Input[1]);
  and and_28 (and_28_out, Input[4], not_67_out, not_68_out, not_69_out);
  and and_29 (and_29_out, not_70_out, not_71_out, not_72_out, Input[0]);
  and and_30 (and_30_out, not_73_out, not_74_out, Input[1], Input[0]);
  and and_31 (and_31_out, not_75_out, Input[3], not_76_out, not_77_out);
  and and_32 (and_32_out, not_78_out, Input[3], Input[2], Input[1]);
  and and_33 (out_6[1], Input[4], not_79_out, not_80_out, not_81_out, not_82_out);
  and and_34 (out_6[0], not_83_out, Input[3], Input[2], Input[1], not_84_out);
  and and_35 (sw_en, not_85_out, Input[3], Input[2], Input[1], Input[0]);
  and and_36 (lw_en, not_86_out, Input[3], Input[2], Input[1], not_87_out);
  and and_37 (eql, not_88_out, Input[3], not_89_out, Input[1], Input[0]);
  and and_38 (neql, not_90_out, Input[3], Input[2], not_91_out, not_92_out);
  and and_39 (jump, not_93_out, Input[3], Input[2], not_94_out, Input[0]);
  and Out (Output, Input[4], not_95_out, not_96_out, not_97_out, Input[0]);
  and u_Out_2 (Output_2, Input[4], not_98_out, not_99_out, not_100_out, not_101_out);
  or or_1 (out_2[4], and_2_out, and_3_out, and_4_out, and_5_out, and_6_out);
  or or_2 (out_2[3], and_7_out, and_8_out, and_9_out, and_10_out, and_11_out);
  or or_3 (out_2[2], and_12_out, and_13_out, and_14_out);
  or or_4 (out_2[1], and_15_out, and_16_out);
  or or_5 (out_2[0], and_17_out, and_18_out);
  or or_6 (or_6_out, and_19_out, and_20_out, and_21_out, and_22_out, and_23_out);
  or or_7 (reg_dst, and_24_out, and_25_out, and_26_out, and_27_out, and_28_out);
  or or_8 (alu_src, and_29_out, and_30_out, and_31_out, and_32_out);
  or or_9 (\wait , Output, Output_2);
  or or_10 (w_en, and_1_out, or_6_out);
endmodule

module clock_manage (
  input  Clock,
  input  Wait_Enable,
  input  Resleae,
  output out_4
);

  wire multiplexer_1_out;

  Multiplexer #(.enable("false")) multiplexer_1 (.in0(Clock), .in1(1'b0), .out(multiplexer_1_out), .sel(Wait_Enable));
  or or_1 (out_4, multiplexer_1_out, Resleae);
endmodule

module Branch (
  input  in_1,
  input  in_2,
  input  in_3,
  output out_4
);

  wire and_1_out, and_2_out, not_1_out;

  and and_1 (and_1_out, in_1, in_2);
  not not_1 (not_1_out, in_2);
  and and_2 (and_2_out, not_1_out, in_3);
  or or_1 (out_4, and_1_out, and_2_out);
endmodule

module _7_segment (
  input  [13:0] in_1,
  input  in_2,
  output [5:0] out_3,
  output [3:0] out_4,
  output [3:0] out_5,
  output [3:0] out_6,
  output [12:0] out_7
);

  wire or_1_out;
  wire [13:0] multiplexer_1_out;

  Multiplexer #(.width(14), .enable("false")) multiplexer_1 (
    .in0({14{1'b0}}), .in1(in_1), .out(multiplexer_1_out), .sel(in_2));
  assign out_7 = {{12{in_2}}, in_2};  // Bit_Extender bit_extender_1
  or or_1 (or_1_out, multiplexer_1_out[7], multiplexer_1_out[8], multiplexer_1_out[9], multiplexer_1_out[10], multiplexer_1_out[11], multiplexer_1_out[12], multiplexer_1_out[13]);
  _3rd_digit u_3rd_digit_1 (.out_2(out_4), .in_1(multiplexer_1_out[6:0]));
  _2nd_last_dig u_2nd_last_dig_1 (.in_1(multiplexer_1_out[6:0]), .out_2(out_5));
  lst_digit lst_digit_1 (.out_2(out_6), .in_1(multiplexer_1_out[6:0]));
  assign out_3 = {{5{or_1_out}}, or_1_out};  // Bit_Extender bit_extender_2
endmodule

module lst_digit (
  input  [6:0] in_1,
  output [3:0] out_2
);

  wire and_1_out, and_2_out, and_3_out, and_4_out, and_5_out, and_6_out, and_7_out, and_8_out, and_9_out,
       and_10_out, and_11_out, and_12_out, and_13_out, and_14_out, and_15_out, and_16_out, and_17_out,
       and_18_out, and_19_out, and_20_out, and_21_out, and_22_out, and_23_out, and_24_out, and_25_out,
       and_26_out, and_27_out, and_28_out, and_29_out, and_30_out, and_31_out, and_32_out, and_33_out,
       and_34_out, and_35_out, and_36_out, and_37_out, and_38_out, and_39_out, and_40_out, and_41_out,
       and_42_out, and_43_out, and_44_out, not_1_out, not_2_out, not_3_out, not_4_out, not_5_out, not_6_out,
       not_7_out, not_8_out, not_9_out, not_10_out, not_11_out, not_12_out, not_13_out, not_14_out,
       not_15_out, not_16_out, not_17_out, not_18_out, not_19_out, not_20_out, not_21_out, not_22_out,
       not_23_out, not_24_out, not_25_out, not_26_out, not_27_out, not_28_out, not_29_out, not_30_out,
       not_31_out, not_32_out, not_33_out, not_34_out, not_35_out, not_36_out, not_37_out, not_38_out,
       not_39_out, not_40_out, not_41_out, not_42_out, not_43_out, not_44_out, not_45_out, not_46_out,
       not_47_out, not_48_out, not_49_out, not_50_out, not_51_out, not_52_out, not_53_out, not_54_out,
       not_55_out, not_56_out, not_57_out, not_58_out, not_59_out, not_60_out, not_61_out, not_62_out,
       not_63_out, not_64_out, not_65_out, not_66_out, not_67_out, not_68_out, not_69_out, not_70_out,
       not_71_out, not_72_out, not_73_out, not_74_out, not_75_out, not_76_out, not_77_out, not_78_out,
       not_79_out, not_80_out, not_81_out, not_82_out, not_83_out, not_84_out, not_85_out, not_86_out,
       not_87_out, not_88_out, not_89_out, not_90_out, not_91_out, not_92_out, not_93_out, not_94_out,
       not_95_out, not_96_out, not_97_out, not_98_out, not_99_out, not_100_out, not_101_out, not_102_out,
       not_103_out, not_104_out, not_105_out, not_106_out, not_107_out, not_108_out, not_109_out,
       not_110_out, not_111_out, not_112_out, not_113_out, not_114_out, not_115_out, not_116_out,
       not_117_out, not_118_out, not_119_out, not_120_out;

  not not_1 (not_1_out, in_1[6]);
  not not_2 (not_2_out, in_1[5]);
  not not_3 (not_3_out, in_1[4]);
  not not_4 (not_4_out, in_1[2]);
  not not_5 (not_5_out, in_1[1]);
  not not_6 (not_6_out, in_1[6]);
  not not_7 (not_7_out, in_1[5]);
  not not_8 (not_8_out, in_1[3]);
  not not_9 (not_9_out, in_1[2]);
  not not_10 (not_10_out, in_1[6]);
  not not_11 (not_11_out, in_1[5]);
  not not_12 (not_12_out, in_1[1]);
  not not_13 (not_13_out, in_1[6]);
  not not_14 (not_14_out, in_1[4]);
  not not_15 (not_15_out, in_1[3]);
  not not_16 (not_16_out, in_1[6]);
  not not_17 (not_17_out, in_1[3]);
  not not_18 (not_18_out, in_1[2]);
  not not_19 (not_19_out, in_1[1]);
  not not_20 (not_20_out, in_1[6]);
  not not_21 (not_21_out, in_1[2]);
  not not_22 (not_22_out, in_1[5]);
  not not_23 (not_23_out, in_1[4]);
  not not_24 (not_24_out, in_1[3]);
  not not_25 (not_25_out, in_1[1]);
  not not_26 (not_26_out, in_1[5]);
  not not_27 (not_27_out, in_1[4]);
  not not_28 (not_28_out, in_1[5]);
  not not_29 (not_29_out, in_1[2]);
  not not_30 (not_30_out, in_1[1]);
  not not_31 (not_31_out, in_1[4]);
  not not_32 (not_32_out, in_1[3]);
  not not_33 (not_33_out, in_1[2]);
  not not_34 (not_34_out, in_1[4]);
  not not_35 (not_35_out, in_1[1]);
  not not_36 (not_36_out, in_1[3]);
  not not_37 (not_37_out, in_1[6]);
  not not_38 (not_38_out, in_1[5]);
  not not_39 (not_39_out, in_1[4]);
  not not_40 (not_40_out, in_1[3]);
  not not_41 (not_41_out, in_1[6]);
  not not_42 (not_42_out, in_1[4]);
  not not_43 (not_43_out, in_1[6]);
  not not_44 (not_44_out, in_1[5]);
  not not_45 (not_45_out, in_1[2]);
  not not_46 (not_46_out, in_1[1]);
  not not_47 (not_47_out, in_1[6]);
  not not_48 (not_48_out, in_1[5]);
  not not_49 (not_49_out, in_1[2]);
  not not_50 (not_50_out, in_1[6]);
  not not_51 (not_51_out, in_1[2]);
  not not_52 (not_52_out, in_1[1]);
  not not_53 (not_53_out, in_1[6]);
  not not_54 (not_54_out, in_1[4]);
  not not_55 (not_55_out, in_1[3]);
  not not_56 (not_56_out, in_1[2]);
  not not_57 (not_57_out, in_1[6]);
  not not_58 (not_58_out, in_1[4]);
  not not_59 (not_59_out, in_1[1]);
  not not_60 (not_60_out, in_1[6]);
  not not_61 (not_61_out, in_1[3]);
  not not_62 (not_62_out, in_1[5]);
  not not_63 (not_63_out, in_1[4]);
  not not_64 (not_64_out, in_1[3]);
  not not_65 (not_65_out, in_1[2]);
  not not_66 (not_66_out, in_1[4]);
  not not_67 (not_67_out, in_1[2]);
  not not_68 (not_68_out, in_1[5]);
  not not_69 (not_69_out, in_1[4]);
  not not_70 (not_70_out, in_1[1]);
  not not_71 (not_71_out, in_1[5]);
  not not_72 (not_72_out, in_1[3]);
  not not_73 (not_73_out, in_1[4]);
  not not_74 (not_74_out, in_1[2]);
  not not_75 (not_75_out, in_1[1]);
  not not_76 (not_76_out, in_1[3]);
  not not_77 (not_77_out, in_1[2]);
  not not_78 (not_78_out, in_1[1]);
  not not_79 (not_79_out, in_1[5]);
  not not_80 (not_80_out, in_1[4]);
  not not_81 (not_81_out, in_1[3]);
  not not_82 (not_82_out, in_1[2]);
  not not_83 (not_83_out, in_1[6]);
  not not_84 (not_84_out, in_1[5]);
  not not_85 (not_85_out, in_1[3]);
  not not_86 (not_86_out, in_1[5]);
  not not_87 (not_87_out, in_1[4]);
  not not_88 (not_88_out, in_1[1]);
  not not_89 (not_89_out, in_1[6]);
  not not_90 (not_90_out, in_1[5]);
  not not_91 (not_91_out, in_1[3]);
  not not_92 (not_92_out, in_1[2]);
  not not_93 (not_93_out, in_1[1]);
  not not_94 (not_94_out, in_1[6]);
  not not_95 (not_95_out, in_1[5]);
  not not_96 (not_96_out, in_1[2]);
  not not_97 (not_97_out, in_1[4]);
  not not_98 (not_98_out, in_1[3]);
  not not_99 (not_99_out, in_1[2]);
  not not_100 (not_100_out, in_1[1]);
  not not_101 (not_101_out, in_1[6]);
  not not_102 (not_102_out, in_1[3]);
  not not_103 (not_103_out, in_1[1]);
  not not_104 (not_104_out, in_1[4]);
  not not_105 (not_105_out, in_1[2]);
  not not_106 (not_106_out, in_1[6]);
  not not_107 (not_107_out, in_1[6]);
  not not_108 (not_108_out, in_1[2]);
  not not_109 (not_109_out, in_1[1]);
  not not_110 (not_110_out, in_1[5]);
  not not_111 (not_111_out, in_1[4]);
  not not_112 (not_112_out, in_1[1]);
  not not_113 (not_113_out, in_1[5]);
  not not_114 (not_114_out, in_1[1]);
  not not_115 (not_115_out, in_1[5]);
  not not_116 (not_116_out, in_1[3]);
  not not_117 (not_117_out, in_1[4]);
  not not_118 (not_118_out, in_1[3]);
  not not_119 (not_119_out, in_1[3]);
  not not_120 (not_120_out, in_1[1]);
  and and_1 (and_1_out, not_1_out, not_2_out, not_3_out, in_1[3], not_4_out, not_5_out);
  and and_2 (and_2_out, not_6_out, not_7_out, in_1[4], not_8_out, not_9_out, in_1[1]);
  and and_3 (and_3_out, not_10_out, not_11_out, in_1[4], in_1[3], in_1[2], not_12_out);
  and and_4 (and_4_out, not_13_out, in_1[5], not_14_out, not_15_out, in_1[2], in_1[1]);
  and and_5 (and_5_out, not_16_out, in_1[5], in_1[4], not_17_out, not_18_out, not_19_out);
  and and_6 (and_6_out, not_20_out, in_1[5], in_1[4], in_1[3], not_21_out, in_1[1]);
  and and_7 (and_7_out, in_1[6], not_22_out, not_23_out, not_24_out, in_1[2], not_25_out);
  and and_8 (and_8_out, in_1[6], not_26_out, not_27_out, in_1[3], in_1[2], in_1[1]);
  and and_9 (and_9_out, in_1[6], not_28_out, in_1[4], in_1[3], not_29_out, not_30_out);
  and and_10 (and_10_out, in_1[6], in_1[5], not_31_out, not_32_out, not_33_out, in_1[1]);
  and and_11 (and_11_out, in_1[6], in_1[5], not_34_out, in_1[3], in_1[2], not_35_out);
  and and_12 (and_12_out, in_1[6], in_1[5], in_1[4], not_36_out, in_1[2], in_1[1]);
  and and_13 (and_13_out, not_37_out, not_38_out, not_39_out, not_40_out, in_1[2]);
  and and_14 (and_14_out, not_41_out, not_42_out, in_1[3], in_1[2], in_1[1]);
  and and_15 (and_15_out, not_43_out, not_44_out, in_1[4], not_45_out, not_46_out);
  and and_16 (and_16_out, not_47_out, not_48_out, in_1[4], in_1[3], not_49_out);
  and and_17 (and_17_out, not_50_out, in_1[4], in_1[3], not_51_out, not_52_out);
  and and_18 (and_18_out, not_53_out, in_1[5], not_54_out, not_55_out, not_56_out, in_1[1]);
  and and_19 (and_19_out, not_57_out, in_1[5], not_58_out, in_1[2], not_59_out);
  and and_20 (and_20_out, not_60_out, in_1[5], in_1[4], not_61_out, in_1[2], in_1[1]);
  and and_21 (and_21_out, in_1[6], not_62_out, not_63_out, not_64_out, not_65_out);
  and and_22 (and_22_out, in_1[6], not_66_out, in_1[3], not_67_out, in_1[1]);
  and and_23 (and_23_out, in_1[6], not_68_out, not_69_out, in_1[3], in_1[2], not_70_out);
  and and_24 (and_24_out, in_1[6], not_71_out, in_1[4], not_72_out, in_1[2]);
  and and_25 (and_25_out, in_1[6], in_1[4], in_1[3], in_1[2], in_1[1]);
  and and_26 (and_26_out, in_1[6], in_1[5], not_73_out, not_74_out, not_75_out);
  and and_27 (and_27_out, in_1[6], in_1[5], in_1[4], not_76_out, not_77_out, in_1[1]);
  and and_28 (and_28_out, in_1[6], in_1[5], in_1[4], in_1[2], not_78_out);
  and and_29 (and_29_out, not_79_out, not_80_out, not_81_out, not_82_out, in_1[1]);
  and and_30 (and_30_out, not_83_out, not_84_out, not_85_out, in_1[2], in_1[1]);
  and and_31 (and_31_out, not_86_out, not_87_out, in_1[3], in_1[2], not_88_out);
  and and_32 (and_32_out, not_89_out, not_90_out, in_1[4], not_91_out, not_92_out, not_93_out);
  and and_33 (and_33_out, not_94_out, not_95_out, in_1[4], in_1[3], not_96_out, in_1[1]);
  and and_34 (and_34_out, in_1[5], not_97_out, not_98_out, not_99_out, not_100_out);
  and and_35 (and_35_out, not_101_out, in_1[5], not_102_out, in_1[2], not_103_out);
  and and_36 (and_36_out, in_1[5], not_104_out, in_1[3], not_105_out, in_1[1]);
  and and_37 (and_37_out, not_106_out, in_1[5], in_1[3], in_1[2], in_1[1]);
  and and_38 (and_38_out, not_107_out, in_1[5], in_1[4], in_1[3], not_108_out, not_109_out);
  and and_39 (and_39_out, in_1[6], not_110_out, not_111_out, in_1[3], not_112_out);
  and and_40 (and_40_out, in_1[6], not_113_out, in_1[3], in_1[2], not_114_out);
  and and_41 (and_41_out, in_1[6], not_115_out, in_1[4], not_116_out, in_1[1]);
  and and_42 (and_42_out, in_1[6], in_1[5], not_117_out, not_118_out, in_1[2], in_1[1]);
  and and_43 (and_43_out, in_1[6], in_1[5], in_1[4], not_119_out, not_120_out);
  and and_44 (and_44_out, in_1[6], in_1[5], in_1[4], in_1[3], in_1[1]);
  or or_1 (out_2[3], and_1_out, and_2_out, and_3_out, and_4_out, and_5_out, and_6_out, and_7_out, and_8_out, and_9_out, and_10_out, and_11_out, and_12_out);
  or or_2 (out_2[2], and_13_out, and_14_out, and_15_out, and_16_out, and_17_out, and_18_out, and_19_out, and_20_out, and_21_out, and_22_out, and_23_out, and_24_out, and_25_out, and_26_out, and_27_out, and_28_out);
  or or_3 (out_2[1], and_29_out, and_30_out, and_31_out, and_32_out, and_33_out, and_34_out, and_35_out, and_36_out, and_37_out, and_38_out, and_39_out, and_40_out, and_41_out, and_42_out, and_43_out, and_44_out);

  assign out_2[0] = in_1[0];
endmodule

module _2nd_last_dig (
  input  [6:0] in_1,
  output [3:0] out_2
);

  wire and_1_out, and_2_out, and_3_out, and_4_out, and_5_out, and_6_out, and_7_out, and_8_out, and_9_out,
       and_10_out, and_11_out, and_12_out, and_13_out, and_14_out, and_15_out, and_16_out, and_17_out,
       and_18_out, and_19_out, and_20_out, and_21_out, and_22_out, and_23_out, and_24_out, and_25_out,
       not_1_out, not_2_out, not_3_out, not_4_out, not_5_out, not_6_out, not_7_out, not_8_out, not_9_out,
       not_10_out, not_11_out, not_12_out, not_13_out, not_14_out, not_15_out, not_16_out, not_17_out,
       not_18_out, not_19_out, not_20_out, not_21_out, not_22_out, not_23_out, not_24_out, not_25_out,
       not_26_out, not_27_out, not_28_out, not_29_out, not_30_out, not_31_out, not_32_out, not_33_out,
       not_34_out, not_35_out, not_36_out, not_37_out, not_38_out, not_39_out, not_40_out, not_41_out,
       not_42_out, not_43_out, not_44_out;

  not not_1 (not_1_out, in_1[5]);
  not not_2 (not_2_out, in_1[4]);
  not not_3 (not_3_out, in_1[3]);
  not not_4 (not_4_out, in_1[2]);
  not not_5 (not_5_out, in_1[6]);
  and and_1 (and_1_out, not_5_out, in_1[5], in_1[3]);
  not not_6 (not_6_out, in_1[6]);
  and and_2 (and_2_out, not_6_out, in_1[5], in_1[4]);
  and and_3 (and_3_out, in_1[6], not_7_out, not_8_out);
  not not_7 (not_7_out, in_1[5]);
  not not_8 (not_8_out, in_1[4]);
  not not_9 (not_9_out, in_1[6]);
  not not_10 (not_10_out, in_1[5]);
  not not_11 (not_11_out, in_1[6]);
  not not_12 (not_12_out, in_1[5]);
  not not_13 (not_13_out, in_1[6]);
  not not_14 (not_14_out, in_1[6]);
  not not_15 (not_15_out, in_1[4]);
  not not_16 (not_16_out, in_1[3]);
  not not_17 (not_17_out, in_1[5]);
  not not_18 (not_18_out, in_1[4]);
  not not_19 (not_19_out, in_1[5]);
  not not_20 (not_20_out, in_1[4]);
  not not_21 (not_21_out, in_1[5]);
  not not_22 (not_22_out, in_1[4]);
  not not_23 (not_23_out, in_1[5]);
  not not_24 (not_24_out, in_1[6]);
  not not_25 (not_25_out, in_1[5]);
  not not_26 (not_26_out, in_1[3]);
  not not_27 (not_27_out, in_1[2]);
  not not_28 (not_28_out, in_1[4]);
  not not_29 (not_29_out, in_1[3]);
  not not_30 (not_30_out, in_1[2]);
  not not_31 (not_31_out, in_1[3]);
  not not_32 (not_32_out, in_1[2]);
  not not_33 (not_33_out, in_1[6]);
  not not_34 (not_34_out, in_1[3]);
  not not_35 (not_35_out, in_1[6]);
  not not_36 (not_36_out, in_1[2]);
  not not_37 (not_37_out, in_1[5]);
  not not_38 (not_38_out, in_1[4]);
  not not_39 (not_39_out, in_1[5]);
  not not_40 (not_40_out, in_1[4]);
  not not_41 (not_41_out, in_1[5]);
  not not_42 (not_42_out, in_1[5]);
  not not_43 (not_43_out, in_1[4]);
  not not_44 (not_44_out, in_1[3]);
  and and_4 (and_4_out, in_1[6], not_1_out, in_1[4]);
  or or_1 (out_2[3], and_4_out, and_5_out);
  and and_5 (and_5_out, in_1[6], in_1[5], not_2_out, not_3_out, not_4_out);
  or or_2 (out_2[2], and_1_out, and_2_out, and_3_out);
  and and_6 (and_6_out, not_9_out, not_10_out, in_1[4], in_1[2]);
  and and_7 (and_7_out, not_11_out, not_12_out, in_1[4], in_1[3]);
  and and_8 (and_8_out, not_13_out, in_1[4], in_1[3], in_1[2]);
  and and_9 (and_9_out, not_14_out, in_1[5], not_15_out, not_16_out);
  and and_10 (and_10_out, in_1[6], not_17_out, not_18_out);
  and and_11 (and_11_out, in_1[6], in_1[5], in_1[4], in_1[3]);
  and and_12 (and_12_out, not_19_out, not_20_out, in_1[3], in_1[1]);
  and and_13 (and_13_out, not_21_out, not_22_out, in_1[3], in_1[2]);
  and and_14 (and_14_out, not_23_out, in_1[3], in_1[2], in_1[1]);
  and and_15 (and_15_out, not_24_out, not_25_out, in_1[4], not_26_out, not_27_out);
  and and_16 (and_16_out, in_1[5], not_28_out, not_29_out, not_30_out);
  and and_17 (and_17_out, in_1[5], not_31_out, not_32_out, in_1[1]);
  and and_18 (and_18_out, not_33_out, in_1[5], not_34_out, in_1[2]);
  and and_19 (and_19_out, not_35_out, in_1[5], in_1[4], in_1[3], not_36_out);
  and and_20 (and_20_out, in_1[6], not_37_out, not_38_out, in_1[2], in_1[1]);
  and and_21 (and_21_out, in_1[6], not_39_out, not_40_out, in_1[3]);
  and and_22 (and_22_out, in_1[6], not_41_out, in_1[3], in_1[1]);
  and and_23 (and_23_out, in_1[6], not_42_out, in_1[3], in_1[2]);
  and and_24 (and_24_out, in_1[6], not_43_out, in_1[3], in_1[2], in_1[1]);
  and and_25 (and_25_out, in_1[6], in_1[5], in_1[4], not_44_out);
  or or_3 (out_2[1], and_6_out, and_7_out, and_8_out, and_9_out, and_10_out, and_11_out);
  or or_4 (out_2[0], and_12_out, and_13_out, and_14_out, and_15_out, and_16_out, and_17_out, and_18_out, and_19_out, and_20_out, and_21_out, and_22_out, and_23_out, and_24_out, and_25_out);
endmodule

module _3rd_digit (
  input  [6:0] in_1,
  output [3:0] out_2
);

  wire and_1_out, and_2_out, and_3_out;

  and and_1 (and_1_out, in_1[6], in_1[5], in_1[2]);
  and and_2 (and_2_out, in_1[6], in_1[5], in_1[3]);
  or or_1 (out_2[0], and_1_out, and_2_out, and_3_out);
  and and_3 (and_3_out, in_1[6], in_1[5], in_1[4]);

  assign out_2[3:1] = 3'b000;
endmodule
